# Fritzing sketch esp32 fil rouge 2025 vpublie (saved by Fritzing 0.9.3b)
breadboards: 1

parts:
  V1 = DC Power [voltage=12V]
  R1 = Resistor [tolerance=±5% resistance=100 package=THT]
  Composant1 = EasyDriver_v44 [part_number=MOTORDRIVER]
  U1 = 74HC595 [part_number=ESP32 package="DIP16 [THT]"]
  Q1 = Basic FET N-Channel [package="DPak [SMD]"]
  M1 = DC Motor
  R2 = Resistor [tolerance=±5% resistance=100k package=THT]
  C1 = Electrolytic Capacitor [capacitance=0.1mF package="100 mil [THT, electrolytic]"]
  C2 = Ceramic Capacitor [capacitance=100nF package="100 mil [THT, multilayer]"]
  D1 = Rectifier Diode [part_number=1N4001 package="300 mil [THT]"]
  M3 = Stepper Motor - Bipolar

nets (from the schematic view):
  N1: V1.V+, V1.V-, Composant1.GND, Composant1.V+, U1.Q1, U1.Q2, U1.Q3, Q1.drain, Q1.source, M1.pin_1, M1.pin_2, R2.Pin_0, C1.-, C2.0, D1.cathode, D1.anode
  N2: R1.Pin_0, U1.Q4
  N3: R1.Pin_1, Q1.Gate, R2.Pin_1
  N4: Composant1.STEP, U1.Q6, U1.Q7, U1.GND
  N5: Composant1.DIR, U1.Q7', U1.MR
  N6: Composant1.OUT2A, M3.C
  N7: Composant1.OUT2B, M3.A
  N8: Composant1.OUT1A, M3.B
  N9: Composant1.OUT1B, M3.D
  N10: U1.DS, U1.Q0, U1.VCC

notes:
  Puce ESP32-Supermini OLED (dans schema U1ESP32)
